// Logisim project SAP_project.circ as structural Verilog: 11 circuits, main circuit main
module main (
  input  in_1,
  input  in_2,
  input  in_3,
  input  in_4,
  input  in_5,
  input  in_6,
  input  in_7,
  input  in_8,
  input  [7:0] in_9,
  input  in_10,
  output [7:0] out_11,
  output [7:0] out_12,
  output [7:0] out_13,
  output [7:0] out_14,
  output [7:0] out_15,
  output [7:0] out_16,
  output [7:0] out_17,
  output [7:0] out_18,
  output [7:0] out_19,
  output [7:0] out_20,
  output [7:0] out_21,
  output [7:0] out_22,
  output [7:0] out_23,
  output [7:0] out_24,
  output [7:0] out_25,
  output [7:0] out_26,
  output [7:0] out_27,
  output [7:0] out_28,
  output [7:0] out_29,
  output [7:0] out_30,
  output [3:0] out_31,
  output T6,
  output T5,
  output T4,
  output [7:0] out_35,
  output T3,
  output T2,
  output T1,
  output HALT
);

  wire a_in, a_out, alu_out, alu_sub, b_in, ins_reg_in_en, ins_reg_out_en, mar_in_en, not_1_out, o_in, o_out,
       pc_en, pc_out, sram_rd, sram_wr;
  wire [3:0] ins_reg_1_ins_out;

  RAM_1 ram_1_1 (
    .sram_rd(sram_rd), .sram_wr(sram_wr), .sram_d_in({out_35[7:4], out_31}),
    .mar_d_in({out_35[7:4], out_31}), .mar_in_en(mar_in_en), .sram_clk(in_7),
    .sram_d_out({out_35[7:4], out_31}), .out_8(out_14), .out_9(out_15), .out_10(out_16), .out_11(out_17),
    .out_12(out_18), .out_13(out_19), .out_14(out_20), .out_15(out_21), .out_16(out_22), .out_17(out_23),
    .out_18(out_25), .out_19(out_26), .out_20(out_27), .out_21(out_28), .out_22(out_29), .out_23(out_30));
  PC_GP pc_gp_1 (.pc_en(pc_en), .pc_clk(in_7), .pc_reset(in_6), .pc_out_en(pc_out), .pc_out(out_31));
  not not_1 (not_1_out, in_8);
  assign {out_35[7:4], out_31} = in_8 ? in_9 : 8'bz;  // Controlled_Buffer controlled_buffer_1
  REG_GP reg_gp_1 (
    .reg_in({out_35[7:4], out_31}), .reg_in_en(a_in), .reg_clk(in_7), .reg_out_en(a_out),
    .reg_int_out(out_11), .reg_out({out_35[7:4], out_31}));
  REG_GP reg_gp_2 (
    .reg_in({out_35[7:4], out_31}), .reg_in_en(b_in), .reg_clk(in_7), .reg_out_en(in_1),
    .reg_int_out(out_24), .reg_out({out_35[7:4], out_31}));
  ins_reg ins_reg_1 (
    .ins_reg_in({out_35[7:4], out_31}), .ins_reg_in_en(ins_reg_in_en), .clk(in_7),
    .ins_reg_out_en(ins_reg_out_en), .adds_out(out_31), .ins_out(ins_reg_1_ins_out));
  ALU alu_1 (
    .ALU_IN_1(out_11), .ALU_OUT_EN(alu_out), .ALU_SUB(alu_sub), .ALU_IN_2(out_24), .ALU_OUT(out_12));  // open: ALU_CARRY_OUT
  CS cs_1 (
    .CLK(in_7), .CLR(in_10), .I7_I6_I5_I4(ins_reg_1_ins_out), .Cp_en(not_1_out), .LI_en(not_1_out),
    .La_en(not_1_out), .Eo_en(not_1_out), .Ep_en(not_1_out), .Lm_en(not_1_out), .CE_en(not_1_out),
    .Lo_en(not_1_out), .Su_en(not_1_out), .RI_en(not_1_out), .Lb_en(not_1_out), .EI_en(not_1_out),
    .Ea_en(not_1_out), .Eu_en(not_1_out), .T6(T6), .T5(T5), .T4(T4), .T3(T3), .T2(T2), .T1(T1), .Cp(pc_en),
    .Ep(pc_out), .CE(sram_rd), .LI(ins_reg_in_en), .EI(ins_reg_out_en), .HLT(HALT), .Lm(mar_in_en),
    .La(a_in), .Lo(o_in), .Ea(a_out), .Su(alu_sub), .Eu(alu_out), .RI(sram_wr), .Lb(b_in), .Eo(o_out));
  assign sram_wr = in_3 ? in_2 : 1'bz;  // Controlled_Buffer controlled_buffer_2
  assign mar_in_en = in_5 ? in_4 : 1'bz;  // Controlled_Buffer controlled_buffer_3
  REG_GP reg_gp_3 (
    .reg_in(out_12), .reg_in_en(o_in), .reg_clk(in_7), .reg_out_en(o_out), .reg_int_out(out_13),
    .reg_out({out_35[7:4], out_31}));

  assign out_35[3:0] = out_31;

  // Other names for the same wires on the sheet: b_out = in_1; clk = in_7; clr = in_10; debug = in_8;
  //   debug_data[7:0] = in_9; pc_reset = in_6

  // Notes on the sheet:
  //   Debug&Testing
endmodule

module ALU (
  input  [7:0] ALU_IN_1,
  input  ALU_OUT_EN,
  input  ALU_SUB,
  input  [7:0] ALU_IN_2,
  output [7:0] ALU_OUT,
  output ALU_CARRY_OUT
);

  wire adder_2_cout, adder_3_cout, adder_4_cout, adder_5_cout, adder_6_cout, adder_7_cout, adder_8_cout,
       xor_1_out, xor_2_out, xor_3_out, xor_4_out, xor_5_out, xor_6_out, xor_7_out, xor_8_out;
  wire [7:0] adder_8_out;

  xor xor_1 (xor_1_out, ALU_IN_2[7], ALU_SUB);
  Adder #(.width(1)) adder_1 (
    .a(ALU_IN_1[7]), .b(xor_1_out), .out(adder_8_out[7]), .cin(adder_2_cout), .cout(ALU_CARRY_OUT));
  Adder #(.width(1)) adder_2 (
    .a(ALU_IN_1[6]), .b(xor_2_out), .out(adder_8_out[6]), .cin(adder_3_cout), .cout(adder_2_cout));
  xor xor_2 (xor_2_out, ALU_IN_2[6], ALU_SUB);
  xor xor_3 (xor_3_out, ALU_IN_2[5], ALU_SUB);
  Adder #(.width(1)) adder_3 (
    .a(ALU_IN_1[5]), .b(xor_3_out), .out(adder_8_out[5]), .cin(adder_4_cout), .cout(adder_3_cout));
  xor xor_4 (xor_4_out, ALU_IN_2[4], ALU_SUB);
  Adder #(.width(1)) adder_4 (
    .a(ALU_IN_1[4]), .b(xor_4_out), .out(adder_8_out[4]), .cin(adder_5_cout), .cout(adder_4_cout));
  Adder #(.width(1)) adder_5 (
    .a(ALU_IN_1[3]), .b(xor_5_out), .out(adder_8_out[3]), .cin(adder_6_cout), .cout(adder_5_cout));
  xor xor_5 (xor_5_out, ALU_IN_2[3], ALU_SUB);
  xor xor_6 (xor_6_out, ALU_IN_2[2], ALU_SUB);
  Adder #(.width(1)) adder_6 (
    .a(ALU_IN_1[2]), .b(xor_6_out), .out(adder_8_out[2]), .cin(adder_7_cout), .cout(adder_6_cout));
  xor xor_7 (xor_7_out, ALU_IN_2[1], ALU_SUB);
  Adder #(.width(1)) adder_7 (
    .a(ALU_IN_1[1]), .b(xor_7_out), .out(adder_8_out[1]), .cin(adder_8_cout), .cout(adder_7_cout));
  xor xor_8 (xor_8_out, ALU_IN_2[0], ALU_SUB);
  Adder #(.width(1)) adder_8 (.a(ALU_IN_1[0]), .b(xor_8_out), .out(adder_8_out[0]), .cin(ALU_SUB), .cout(adder_8_cout));
  assign ALU_OUT = ALU_OUT_EN ? adder_8_out : 8'bz;  // Controlled_Buffer controlled_buffer_1

  // Notes on the sheet:
  //   Input  1
  //   Carry Out
  //   Substract Control
  //   Input 2
  //   Full Adders
  //   Output Control
  //   ALU Output
endmodule

module REG_GP (
  input  [7:0] reg_in,
  input  reg_in_en,
  input  reg_clk,
  input  reg_out_en,
  output [7:0] reg_int_out,
  output [7:0] reg_out
);

  wire multiplexer_1_out, multiplexer_2_out, multiplexer_3_out, multiplexer_4_out, multiplexer_5_out,
       multiplexer_6_out, multiplexer_7_out, multiplexer_8_out;

  Multiplexer multiplexer_1 (.in0(reg_int_out[7]), .in1(reg_in[7]), .out(multiplexer_1_out), .sel(reg_in_en));
  D_Flip_Flop d_ff_1 (.D(multiplexer_1_out), .clk(reg_clk), .Q(reg_int_out[7]));  // open: Qn, preset, reset
  assign reg_out[7] = reg_out_en ? reg_int_out[7] : 1'bz;  // Controlled_Buffer controlled_buffer_1
  Multiplexer multiplexer_2 (.in0(reg_int_out[6]), .in1(reg_in[6]), .out(multiplexer_2_out), .sel(reg_in_en));
  D_Flip_Flop d_ff_2 (.D(multiplexer_2_out), .clk(reg_clk), .Q(reg_int_out[6]));  // open: Qn, preset, reset
  assign reg_out[6] = reg_out_en ? reg_int_out[6] : 1'bz;  // Controlled_Buffer controlled_buffer_2
  Multiplexer multiplexer_3 (.in0(reg_int_out[5]), .in1(reg_in[5]), .out(multiplexer_3_out), .sel(reg_in_en));
  D_Flip_Flop d_ff_3 (.D(multiplexer_3_out), .clk(reg_clk), .Q(reg_int_out[5]));  // open: Qn, preset, reset
  assign reg_out[5] = reg_out_en ? reg_int_out[5] : 1'bz;  // Controlled_Buffer controlled_buffer_3
  Multiplexer multiplexer_4 (.in0(reg_int_out[4]), .in1(reg_in[4]), .out(multiplexer_4_out), .sel(reg_in_en));
  D_Flip_Flop d_ff_4 (.D(multiplexer_4_out), .clk(reg_clk), .Q(reg_int_out[4]));  // open: Qn, preset, reset
  Multiplexer multiplexer_5 (.in0(reg_int_out[3]), .in1(reg_in[3]), .out(multiplexer_5_out), .sel(reg_in_en));
  assign reg_out[4] = reg_out_en ? reg_int_out[4] : 1'bz;  // Controlled_Buffer controlled_buffer_4
  D_Flip_Flop d_ff_5 (.D(multiplexer_5_out), .clk(reg_clk), .Q(reg_int_out[3]));  // open: Qn, preset, reset
  assign reg_out[3] = reg_out_en ? reg_int_out[3] : 1'bz;  // Controlled_Buffer controlled_buffer_5
  Multiplexer multiplexer_6 (.in0(reg_int_out[2]), .in1(reg_in[2]), .out(multiplexer_6_out), .sel(reg_in_en));
  D_Flip_Flop d_ff_6 (.D(multiplexer_6_out), .clk(reg_clk), .Q(reg_int_out[2]));  // open: Qn, preset, reset
  assign reg_out[2] = reg_out_en ? reg_int_out[2] : 1'bz;  // Controlled_Buffer controlled_buffer_6
  Multiplexer multiplexer_7 (.in0(reg_int_out[1]), .in1(reg_in[1]), .out(multiplexer_7_out), .sel(reg_in_en));
  D_Flip_Flop d_ff_7 (.D(multiplexer_7_out), .clk(reg_clk), .Q(reg_int_out[1]));  // open: Qn, preset, reset
  assign reg_out[1] = reg_out_en ? reg_int_out[1] : 1'bz;  // Controlled_Buffer controlled_buffer_7
  Multiplexer multiplexer_8 (.in0(reg_int_out[0]), .in1(reg_in[0]), .out(multiplexer_8_out), .sel(reg_in_en));
  D_Flip_Flop d_ff_8 (.D(multiplexer_8_out), .clk(reg_clk), .Q(reg_int_out[0]));  // open: Qn, preset, reset
  assign reg_out[0] = reg_out_en ? reg_int_out[0] : 1'bz;  // Controlled_Buffer controlled_buffer_8

  // Notes on the sheet:
  //   Input
  //   Input Control
  //   Clock
  //   Output Control
  //   Memory
  //   Output
  //    Internal Output
endmodule

module PC_GP (
  input  pc_en,
  input  pc_clk,
  input  pc_reset,
  input  pc_out_en,
  output [3:0] pc_out
);

  wire j_k_ff_2_qn, j_k_ff_3_qn, j_k_ff_4_qn;
  wire [3:0] j_k_ff_4_q;

  J_K_Flip_Flop j_k_ff_1 (
    .J(pc_en), .K(pc_en), .clk(j_k_ff_2_qn), .Q(j_k_ff_4_q[3]), .reset(pc_reset));  // open: Qn, preset
  J_K_Flip_Flop j_k_ff_2 (
    .J(pc_en), .K(pc_en), .clk(j_k_ff_3_qn), .Q(j_k_ff_4_q[2]), .Qn(j_k_ff_2_qn), .reset(pc_reset));  // open: preset
  J_K_Flip_Flop j_k_ff_3 (
    .J(pc_en), .K(pc_en), .clk(j_k_ff_4_qn), .Q(j_k_ff_4_q[1]), .Qn(j_k_ff_3_qn), .reset(pc_reset));  // open: preset
  J_K_Flip_Flop j_k_ff_4 (
    .J(pc_en), .K(pc_en), .clk(pc_clk), .Q(j_k_ff_4_q[0]), .Qn(j_k_ff_4_qn), .reset(pc_reset));  // open: preset
  assign pc_out = pc_out_en ? j_k_ff_4_q : 4'bz;  // Controlled_Buffer controlled_buffer_1

  // Notes on the sheet:
  //   Clock
  //   Reset
  //   Count Control
  //   Output Control
  //   Counter Output
endmodule

module dec_4X16 (
  input  [3:0] dec_sel,
  output [15:0] dec_out
);

  wire not_1_out, not_2_out, not_3_out, not_4_out;

  not not_1 (not_1_out, dec_sel[3]);
  not not_2 (not_2_out, dec_sel[2]);
  not not_3 (not_3_out, dec_sel[1]);
  not not_4 (not_4_out, dec_sel[0]);
  and and_1 (dec_out[1], dec_sel[0], not_3_out, not_2_out, not_1_out);
  and and_2 (dec_out[2], not_4_out, dec_sel[1], not_2_out, not_1_out);
  and and_3 (dec_out[3], dec_sel[0], dec_sel[1], not_2_out, not_1_out);
  and and_4 (dec_out[4], not_4_out, not_3_out, dec_sel[2], not_1_out);
  and and_5 (dec_out[5], dec_sel[0], not_3_out, dec_sel[2], not_1_out);
  and and_6 (dec_out[6], not_4_out, dec_sel[1], dec_sel[2], not_1_out);
  and and_7 (dec_out[7], dec_sel[0], dec_sel[1], dec_sel[2], not_1_out);
  and and_8 (dec_out[8], not_4_out, not_3_out, not_2_out, dec_sel[3]);
  and and_9 (dec_out[9], dec_sel[0], not_3_out, not_2_out, dec_sel[3]);
  and and_10 (dec_out[10], not_4_out, dec_sel[1], not_2_out, dec_sel[3]);
  and and_11 (dec_out[11], dec_sel[0], dec_sel[1], not_2_out, dec_sel[3]);
  and and_12 (dec_out[12], not_4_out, not_3_out, dec_sel[2], dec_sel[3]);
  and and_13 (dec_out[13], dec_sel[0], not_3_out, dec_sel[2], dec_sel[3]);
  and and_14 (dec_out[14], not_4_out, dec_sel[1], dec_sel[2], dec_sel[3]);
  and and_15 (dec_out[15], dec_sel[0], dec_sel[1], dec_sel[2], dec_sel[3]);
  and and_16 (dec_out[0], not_4_out, not_3_out, not_2_out, not_1_out);
endmodule

module SRAM (
  input  [7:0] data_in,
  input  wr_en,
  input  clk,
  input  cs,
  input  rd_en,
  output [7:0] memory_content,
  output [7:0] data_out
);

  wire and_1_out, and_2_out;

  and and_1 (and_1_out, wr_en, cs);
  and and_2 (and_2_out, cs, rd_en);
  REG_GP reg_gp_1 (
    .reg_in(data_in), .reg_in_en(and_1_out), .reg_clk(clk), .reg_out_en(and_2_out),
    .reg_int_out(memory_content), .reg_out(data_out));
endmodule

module ins_reg (
  input  [7:0] ins_reg_in,
  input  ins_reg_in_en,
  input  clk,
  input  ins_reg_out_en,
  output [3:0] adds_out,
  output [3:0] ins_out
);

  wire [3:0] reg_gp_1_reg_int_out;

  REG_GP reg_gp_1 (
    .reg_in(ins_reg_in), .reg_in_en(ins_reg_in_en), .reg_clk(clk),
    .reg_int_out({ins_out, reg_gp_1_reg_int_out}));  // open: reg_out_en, reg_out
  assign adds_out = ins_reg_out_en ? reg_gp_1_reg_int_out : 4'bz;  // Controlled_Buffer controlled_buffer_1
endmodule

module RAM_1 (
  input  sram_rd,
  input  sram_wr,
  input  [7:0] sram_d_in,
  input  [7:0] mar_d_in,
  input  mar_in_en,
  input  sram_clk,
  output [7:0] sram_d_out,
  output [7:0] out_8,
  output [7:0] out_9,
  output [7:0] out_10,
  output [7:0] out_11,
  output [7:0] out_12,
  output [7:0] out_13,
  output [7:0] out_14,
  output [7:0] out_15,
  output [7:0] out_16,
  output [7:0] out_17,
  output [7:0] out_18,
  output [7:0] out_19,
  output [7:0] out_20,
  output [7:0] out_21,
  output [7:0] out_22,
  output [7:0] out_23
);

  wire [7:0] reg_gp_1_reg_int_out, sram_1_data_out;
  wire [15:0] dec_4x16_1_dec_out;

  REG_GP reg_gp_1 (
    .reg_in(mar_d_in), .reg_in_en(mar_in_en), .reg_clk(sram_clk), .reg_int_out(reg_gp_1_reg_int_out));  // open: reg_out_en, reg_out
  dec_4X16 dec_4x16_1 (.dec_sel(reg_gp_1_reg_int_out[3:0]), .dec_out(dec_4x16_1_dec_out));
  SRAM sram_1 (
    .data_in(sram_1_data_out), .wr_en(sram_wr), .clk(sram_clk), .cs(dec_4x16_1_dec_out[0]), .rd_en(sram_rd),
    .memory_content(out_8), .data_out(sram_1_data_out));
  SRAM sram_2 (
    .data_in(sram_1_data_out), .wr_en(sram_wr), .clk(sram_clk), .cs(dec_4x16_1_dec_out[1]), .rd_en(sram_rd),
    .memory_content(out_9), .data_out(sram_1_data_out));
  SRAM sram_3 (
    .data_in(sram_1_data_out), .wr_en(sram_wr), .clk(sram_clk), .cs(dec_4x16_1_dec_out[2]), .rd_en(sram_rd),
    .memory_content(out_10), .data_out(sram_1_data_out));
  SRAM sram_4 (
    .data_in(sram_1_data_out), .wr_en(sram_wr), .clk(sram_clk), .cs(dec_4x16_1_dec_out[3]), .rd_en(sram_rd),
    .memory_content(out_11), .data_out(sram_1_data_out));
  SRAM sram_5 (
    .data_in(sram_1_data_out), .wr_en(sram_wr), .clk(sram_clk), .cs(dec_4x16_1_dec_out[4]), .rd_en(sram_rd),
    .memory_content(out_12), .data_out(sram_1_data_out));
  SRAM sram_6 (
    .data_in(sram_1_data_out), .wr_en(sram_wr), .clk(sram_clk), .cs(dec_4x16_1_dec_out[5]), .rd_en(sram_rd),
    .memory_content(out_13), .data_out(sram_1_data_out));
  SRAM sram_7 (
    .data_in(sram_1_data_out), .wr_en(sram_wr), .clk(sram_clk), .cs(dec_4x16_1_dec_out[6]), .rd_en(sram_rd),
    .memory_content(out_14), .data_out(sram_1_data_out));
  SRAM sram_8 (
    .data_in(sram_1_data_out), .wr_en(sram_wr), .clk(sram_clk), .cs(dec_4x16_1_dec_out[7]), .rd_en(sram_rd),
    .memory_content(out_15), .data_out(sram_1_data_out));
  SRAM sram_9 (
    .data_in(sram_1_data_out), .wr_en(sram_wr), .clk(sram_clk), .cs(dec_4x16_1_dec_out[8]), .rd_en(sram_rd),
    .memory_content(out_16), .data_out(sram_1_data_out));
  SRAM sram_10 (
    .data_in(sram_1_data_out), .wr_en(sram_wr), .clk(sram_clk), .cs(dec_4x16_1_dec_out[9]), .rd_en(sram_rd),
    .memory_content(out_17), .data_out(sram_1_data_out));
  SRAM sram_11 (
    .data_in(sram_1_data_out), .wr_en(sram_wr), .clk(sram_clk), .cs(dec_4x16_1_dec_out[10]), .rd_en(sram_rd),
    .memory_content(out_18), .data_out(sram_1_data_out));
  SRAM sram_12 (
    .data_in(sram_1_data_out), .wr_en(sram_wr), .clk(sram_clk), .cs(dec_4x16_1_dec_out[11]), .rd_en(sram_rd),
    .memory_content(out_19), .data_out(sram_1_data_out));
  SRAM sram_13 (
    .data_in(sram_1_data_out), .wr_en(sram_wr), .clk(sram_clk), .cs(dec_4x16_1_dec_out[12]), .rd_en(sram_rd),
    .memory_content(out_20), .data_out(sram_1_data_out));
  SRAM sram_14 (
    .data_in(sram_1_data_out), .wr_en(sram_wr), .clk(sram_clk), .cs(dec_4x16_1_dec_out[13]), .rd_en(sram_rd),
    .memory_content(out_21), .data_out(sram_1_data_out));
  SRAM sram_15 (
    .data_in(sram_1_data_out), .wr_en(sram_wr), .clk(sram_clk), .cs(dec_4x16_1_dec_out[14]), .rd_en(sram_rd),
    .memory_content(out_22), .data_out(sram_1_data_out));
  SRAM sram_16 (
    .data_in(sram_1_data_out), .wr_en(sram_wr), .clk(sram_clk), .cs(dec_4x16_1_dec_out[15]), .rd_en(sram_rd),
    .memory_content(out_23), .data_out(sram_1_data_out));
  assign sram_1_data_out = sram_wr ? sram_d_in : 8'bz;  // Controlled_Buffer controlled_buffer_1
  assign sram_d_out = sram_rd ? sram_1_data_out : 8'bz;  // Controlled_Buffer controlled_buffer_2
endmodule

module Ring_Counter (
  input  CLK,
  input  CLR,
  output T6,
  output T5,
  output T4,
  output T3,
  output T2,
  output T1
);

  wire j_k_ff_1_qn, j_k_ff_2_qn, j_k_ff_3_qn, j_k_ff_4_qn, j_k_ff_5_qn, j_k_ff_6_qn, not_1_out;

  J_K_Flip_Flop j_k_ff_1 (
    .J(T5), .K(j_k_ff_2_qn), .clk(CLK), .Q(T6), .Qn(j_k_ff_1_qn), .reset(not_1_out));  // open: preset
  J_K_Flip_Flop j_k_ff_2 (
    .J(T4), .K(j_k_ff_3_qn), .clk(CLK), .Q(T5), .Qn(j_k_ff_2_qn), .reset(not_1_out));  // open: preset
  J_K_Flip_Flop j_k_ff_3 (
    .J(T3), .K(j_k_ff_4_qn), .clk(CLK), .Q(T4), .Qn(j_k_ff_3_qn), .reset(not_1_out));  // open: preset
  J_K_Flip_Flop j_k_ff_4 (
    .J(T2), .K(j_k_ff_5_qn), .clk(CLK), .Q(T3), .Qn(j_k_ff_4_qn), .reset(not_1_out));  // open: preset
  J_K_Flip_Flop j_k_ff_5 (
    .J(T1), .K(j_k_ff_6_qn), .clk(CLK), .Q(T2), .Qn(j_k_ff_5_qn), .reset(not_1_out));  // open: preset
  J_K_Flip_Flop j_k_ff_6 (
    .J(T6), .K(j_k_ff_1_qn), .clk(CLK), .Q(T1), .Qn(j_k_ff_6_qn), .preset(not_1_out));  // open: reset
  not not_1 (not_1_out, CLR);
endmodule

module CS (
  input  CLK,
  input  CLR,
  input  [3:0] I7_I6_I5_I4,
  input  Cp_en,
  input  LI_en,
  input  La_en,
  input  Eo_en,
  input  Ep_en,
  input  Lm_en,
  input  CE_en,
  input  Lo_en,
  input  Su_en,
  input  RI_en,
  input  Lb_en,
  input  EI_en,
  input  Ea_en,
  input  Eu_en,
  output T6,
  output T5,
  output T4,
  output T3,
  output T2,
  output T1,
  output Cp,
  output Ep,
  output CE,
  output LI,
  output EI,
  output HLT,
  output Lm,
  output La,
  output Lo,
  output Ea,
  output Su,
  output Eu,
  output RI,
  output Lb,
  output Eo
);

  wire and_1_out, and_2_out, and_3_out, and_4_out, and_5_out, and_6_out, and_7_out, and_8_out, and_9_out,
       and_10_out, and_11_out, and_12_out, and_13_out, and_14_out, and_15_out, and_16_out, and_17_out,
       and_18_out, and_19_out, and_20_out, and_21_out, and_22_out, and_23_out, and_24_out, and_25_out,
       and_26_out, instruction_dec_1_acc_out, instruction_dec_1_add, instruction_dec_1_lda,
       instruction_dec_1_ldb, instruction_dec_1_str, instruction_dec_1_sub, or_1_out, or_2_out, or_3_out,
       or_4_out, or_5_out, or_6_out;

  Instruction_dec instruction_dec_1 (
    .I7(I7_I6_I5_I4[3]), .I6(I7_I6_I5_I4[2]), .I5(I7_I6_I5_I4[1]), .I4(I7_I6_I5_I4[0]),
    .LDA(instruction_dec_1_lda), .ADD(instruction_dec_1_add), .SUB(instruction_dec_1_sub),
    .ACC_OUT(instruction_dec_1_acc_out), .STR(instruction_dec_1_str), .LDB(instruction_dec_1_ldb), .HLT(HLT));
  assign Cp = Cp_en ? T2 : 1'bz;  // Controlled_Buffer controlled_buffer_1
  assign Ep = Ep_en ? T1 : 1'bz;  // Controlled_Buffer controlled_buffer_2
  and and_1 (and_1_out, instruction_dec_1_lda, T4);
  and and_2 (and_2_out, instruction_dec_1_ldb, T4);
  and and_3 (and_3_out, instruction_dec_1_add, T4);
  or or_1 (or_1_out, T1, and_1_out, and_2_out, and_3_out, and_4_out, and_5_out);
  assign Lm = Lm_en ? or_1_out : 1'bz;  // Controlled_Buffer controlled_buffer_3
  Ring_Counter ring_counter_1 (.CLK(CLK), .CLR(CLR), .T6(T6), .T5(T5), .T4(T4), .T3(T3), .T2(T2), .T1(T1));
  and and_4 (and_4_out, instruction_dec_1_sub, T4);
  and and_5 (and_5_out, instruction_dec_1_str, T4);
  and and_6 (and_6_out, instruction_dec_1_lda, T5);
  and and_7 (and_7_out, instruction_dec_1_ldb, T5);
  and and_8 (and_8_out, instruction_dec_1_add, T5);
  or or_2 (or_2_out, T3, and_6_out, and_7_out, and_8_out, and_9_out);
  assign CE = CE_en ? or_2_out : 1'bz;  // Controlled_Buffer controlled_buffer_4
  and and_9 (and_9_out, instruction_dec_1_sub, T5);
  assign LI = LI_en ? T3 : 1'bz;  // Controlled_Buffer controlled_buffer_5
  and and_10 (and_10_out, instruction_dec_1_lda, T4);
  and and_11 (and_11_out, instruction_dec_1_ldb, T4);
  and and_12 (and_12_out, instruction_dec_1_add, T4);
  or or_3 (or_3_out, and_10_out, and_11_out, and_12_out, and_13_out, and_14_out);
  assign EI = EI_en ? or_3_out : 1'bz;  // Controlled_Buffer controlled_buffer_6
  and and_13 (and_13_out, instruction_dec_1_sub, T4);
  and and_14 (and_14_out, instruction_dec_1_str, T4);
  and and_15 (and_15_out, instruction_dec_1_lda, T5);
  assign La = La_en ? and_15_out : 1'bz;  // Controlled_Buffer controlled_buffer_7
  and and_16 (and_16_out, instruction_dec_1_add, T6);
  and and_17 (and_17_out, instruction_dec_1_sub, T6);
  or or_4 (or_4_out, and_16_out, and_17_out);
  assign Lo = Lo_en ? or_4_out : 1'bz;  // Controlled_Buffer controlled_buffer_8
  and and_18 (and_18_out, instruction_dec_1_acc_out, T4);
  assign Ea = Ea_en ? and_18_out : 1'bz;  // Controlled_Buffer controlled_buffer_9
  and and_19 (and_19_out, instruction_dec_1_sub, T6);
  assign Su = Su_en ? and_19_out : 1'bz;  // Controlled_Buffer controlled_buffer_10
  and and_20 (and_20_out, instruction_dec_1_add, T6);
  and and_21 (and_21_out, instruction_dec_1_sub, T6);
  or or_5 (or_5_out, and_20_out, and_21_out);
  assign Eu = Eu_en ? or_5_out : 1'bz;  // Controlled_Buffer controlled_buffer_11
  and and_22 (and_22_out, instruction_dec_1_str, T5);
  assign RI = RI_en ? and_22_out : 1'bz;  // Controlled_Buffer controlled_buffer_12
  and and_23 (and_23_out, instruction_dec_1_ldb, T5);
  and and_24 (and_24_out, instruction_dec_1_add, T5);
  and and_25 (and_25_out, instruction_dec_1_sub, T5);
  or or_6 (or_6_out, and_23_out, and_24_out, and_25_out);
  assign Lb = Lb_en ? or_6_out : 1'bz;  // Controlled_Buffer controlled_buffer_13
  and and_26 (and_26_out, instruction_dec_1_str, T5);
  assign Eo = Eo_en ? and_26_out : 1'bz;  // Controlled_Buffer controlled_buffer_14
endmodule

module Instruction_dec (
  input  I7,
  input  I6,
  input  I5,
  input  I4,
  output LDA,
  output ADD,
  output SUB,
  output ACC_OUT,
  output STR,
  output LDB,
  output HLT
);

  wire and_1_out, and_2_out, and_3_out, and_4_out, and_5_out, and_6_out, and_7_out, not_1_out, not_2_out,
       not_3_out, not_4_out;

  not not_1 (not_1_out, I7);
  not not_2 (not_2_out, I6);
  not not_3 (not_3_out, I5);
  not not_4 (not_4_out, I4);
  and and_1 (and_1_out, not_1_out, not_2_out, not_3_out, I4);
  and and_2 (and_2_out, not_1_out, I6, not_3_out, not_4_out);
  and and_3 (and_3_out, not_1_out, I6, not_3_out, I4);
  and and_4 (and_4_out, not_1_out, I6, I5, not_4_out);
  and and_5 (and_5_out, not_1_out, I6, I5, I4);
  and and_6 (and_6_out, not_1_out, not_2_out, I5, not_4_out);
  and and_7 (and_7_out, I7, I6, I5, I4);
  buf buffer_1 (LDA, and_1_out);
  buf buffer_2 (ADD, and_2_out);
  buf buffer_3 (SUB, and_3_out);
  buf buffer_4 (ACC_OUT, and_4_out);
  buf buffer_5 (STR, and_5_out);
  buf buffer_6 (LDB, and_6_out);
  buf buffer_7 (HLT, and_7_out);
endmodule
